# Fritzing sketch DriverStation (saved by Fritzing 0.9.3b)
breadboards: 1

parts:
  Part1 = Arduino Nano (Rev3.0) (ICSP)
  R1 = Slide Potentiometer [maximum_resistance=100kΩ]
  M1 = DC Motor
  J1 = Screw terminal - 2 pins [package=THT]
  JP1 = Header 8 [package=1x08_smd_alt]
  JP2 = Header 3 [package=screwterminal-3.5mm-3_lock.007s]
  S6 = Square Pushbutton
  R2 = Resistor [tolerance=±5% resistance=220 package="1206 [SMD]"]
  U1 = CAPSENSE_PAD [package=capsense_pad]
  VCC1 = Battery block 9V
  U2 = SWITCH-SPST-2 [package=switch-spst-vertical]
  U3 = SWITCH-SPST-2 [package=switch-spst-vertical]
  U4 = SWITCH-SPST-2 [package=switch-spst-vertical]
  U5 = SWITCH-SPST-2 [package=switch-spst-vertical]
  U6 = SWITCH-SPST-2 [package=switch-spst-vertical]

nets:
  N1: Part1.D2, U6.O
  N2: Part1.D3, U5.O
  N3: Part1.D4, U4.O
  N4: Part1.D5, U3.O
  N5: Part1.D6, U2.O
  N6: Part1.D7, S6.leg0
  N7: Part1.D11/MOSI, R2.Pin_1
  N8: Part1.D12/MISO, R2.Pin_0, U1.RECEIVE
  N9: Part1.GND, R1.leg1, JP2.2, VCC1.-
  N10: Part1.5V, R1.leg2, JP2.1, S6.leg1
  N11: Part1.A0, R1.wiper
  N12: M1.pin_1, J1.pin2
  N13: M1.pin_2, J1.pin1
  N14: JP1.1, JP1.2
  N15: JP1.6, JP1.7, JP1.8

notes:
  L289N Motor Drive Dual H-Bridge DC Motor Control Module for Arduino
  ENB
  ENA
  OUT 1
  OUT 2
  IN2
  IN1
  +12v
  GND
  +5v
  470K
